# Fritzing sketch DaisySeedBlink (saved by Fritzing 0.9.4)
circuit board: 8.46667cm x 5.64444cm
breadboards: 1

parts:
  SOM1 = Daisy Seed [chip_label=IC package="DIP (Dual Inline) [THT]"]
  LED1 = LED - 5mm [color="Red (633nm)" package="5 mm [THT]"]
  R1 = Resistor [tolerance=±5% resistance=1k package=THT]

nets:
  N1: SOM1.pin1, LED1.cathode
  N2: SOM1.pin_20, SOM1.pin_40
  N3: SOM1.pin_38, R1.Pin_1
  N4: LED1.anode, R1.Pin_0

custom parts:
  Daisy Seed: Daisy is an embedded platform for music. It features everything you need for creating high fidelity audio hardware devices. Just plug in a USB cable and start making sound! No soldering required.
